# Fritzing sketch Schematic (saved by Fritzing 0.8.7b)

parts:
  Mod1 = Raspberry Pi 4B
  Part1 = Arduino Uno (Rev3)
  Logic_Level_Converter = Logic Level Converter [part_number=BDLLC]
  BATT1 = LiPoly Battery (1300mAh)
  DC_Motor_Driver = Adafruit DRV8833 DC/Stepper Motor Driver [part_number=DRV8833]
  DCL = Hobby Gearmotor with 48:1 gearbox [part_number=DC2]
  DCR = Hobby Gearmotor with 48:1 gearbox [part_number=DC1]
  Ultrasonic_Sensors = HC-SR04 [part_number=HC-SR04]
  hc-sr2 = HC-SR04
  hc-sr3 = HC-SR04
  Line_Sensors = TCRT5000 digital module [part_number=TCRT5000]
  TCRT3 = TCRT5000 digital module [part_number=151608]
  Servo_Driver = 16-Channel 12-bit PWM Servo Driver - I2C [part_number=PCA9685]
  Stepper_Driver = DRV 8825 Stepper Motor Carrier, High Current [part_number=DRV8834]
  J1 = Basic Servo
  J2 = Basic Servo
  J3 = Basic Servo
  J4 = Basic Servo
  C1 = Ceramic Capacitor [capacitance=100nF package="100 mil [THT, multilayer]"]
  Voltage_Regulator = Voltage Regulator - 5V [part_number=7805 package="TO220 [THT]"]
  Arm_Stepper = Stepper Motor - Unipolar [part_number="Nema 17"]

nets:
  N1: Mod1.3V3, Logic_Level_Converter.LV, Stepper_Driver.SLEEP
  5V: Mod1.5V, Part1.VIN
  N2: Mod1.GPIO2, Logic_Level_Converter.TX_LV
  N3: Mod1.GPIO3, Logic_Level_Converter.RX_LV
  N4: Mod1.GPIO14, Logic_Level_Converter.TX2_LV
  N5: Mod1.GPIO15, Logic_Level_Converter.RX2_LV
  N6: Mod1.GPIO17, Stepper_Driver.STEP
  N7: Mod1.GPIO27, Stepper_Driver.DIRECTION
  GND: Mod1.GPIO23, Part1.GND, Logic_Level_Converter.GND, BATT1.negative, DC_Motor_Driver.GND, Ultrasonic_Sensors.GND, TCRT3.GND, Servo_Driver.GND, Stepper_Driver.GROUND_ST/_MT, Stepper_Driver.GROUND_LOG, J1.gnd, J2.gnd, J3.gnd, J4.gnd, C1.0, Voltage_Regulator.GND
  N8: Part1.D8, hc-sr3.Trig
  N9: Part1.D9_PWM, hc-sr3.Echo
  N10: Part1.D10_PWM/SS, hc-sr2.Trig
  N11: Part1.D11_PWM/MOSI, hc-sr2.Echo
  N12: Part1.D12/MISO, Ultrasonic_Sensors.Trig
  N13: Part1.D13/SCK, Ultrasonic_Sensors.Echo
  N14: Part1.D0/RX, Logic_Level_Converter.TX2_HV
  N15: Part1.D1/TX, Logic_Level_Converter.RX2_HV
  N16: Part1.D2, DC_Motor_Driver.AIN1
  N17: Part1.D3_PWM, DC_Motor_Driver.AIN2
  N18: Part1.D4, DC_Motor_Driver.BIN2
  N19: Part1.D5_PWM, DC_Motor_Driver.BIN1
  N20: Part1.D6_PWM, Line_Sensors.DO1
  N21: Part1.D7, TCRT3.DO1
  VCC: Part1.5V, Logic_Level_Converter.HV, TCRT3.VCC, Servo_Driver.VCC
  N22: Logic_Level_Converter.TX_HV, Servo_Driver.SDA
  N23: Logic_Level_Converter.RX_HV, Servo_Driver.SCL
  N24: BATT1.positive, DC_Motor_Driver.PWRIN, Stepper_Driver.VOLTAGE_ST/_MT, C1.1, Voltage_Regulator.input_voltage
  N25: DC_Motor_Driver.AOUT2, DCL.pin_1
  N26: DC_Motor_Driver.AOUT1, DCL.pin_2
  N27: DC_Motor_Driver.BOUT1, DCR.pin_2
  N28: DC_Motor_Driver.BOUT2, DCR.pin_1
  VCC_2: hc-sr2.VCC, hc-sr3.VCC
  N29: Servo_Driver.PWRIN, Voltage_Regulator.output_voltage
  N30: Servo_Driver.PWM3, J1.pulse
  VCC_3: Servo_Driver.5.0V, J1.vcc, J2.vcc, J3.vcc, J4.vcc
  N31: Servo_Driver.PWM2, J3.pulse
  N32: Servo_Driver.PWM1, J2.pulse
  N33: Servo_Driver.PWM0, J4.pulse
  N34: Stepper_Driver.OUT_2B, Arm_Stepper.D
  N35: Stepper_Driver.OUT_2A, Arm_Stepper.C
  N36: Stepper_Driver.OUT_1A, Arm_Stepper.A
  N37: Stepper_Driver.OUT_1B, Arm_Stepper.B

custom parts:
  LiPoly Battery (1300mAh): Lithium Ion Polymer Battery (1300mAh)
  Adafruit DRV8833 DC/Stepper Motor Driver: Spin two DC motors or step one bi-polar or uni-polar stepper with up to 1.2A per channel using the DRV8833. This motor driver chip is a nice alternative to the TB6612 driver. Like that chip, you get 2 full H-bridges, but this chip is better for low voltage uses (can run from 2.7V up to 10.8V motor power) and has built in current limiting capability. We set it up for 1A current limiting so you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
  HC-SR04: This is a HC-SR04 Distance Sensor. This economical sensor provides 2cm to 400cm of non-contact measurement functionality with a ranging accuracy that can reach up to 3mm. Each HC-SR04 module includes an ultrasonic transmitter, a receiver and a control circuit. There are only four pins that you need to worry about on the HC-SR04: VCC (Power), Trig (Trigger), Echo (Receive), and GND (Ground).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
  TCRT5000 digital module: breakout board for TCRT5000 module, convert analog to digital - Uses TCRT5000 infrared reflectance sensor - Detection distance: 1mm~8mm - Focus distance: 2.5mm - Working voltage: 3.3V~12V - Uses wide voltage LM393 comparator - With multi-turn precision potentiometer to adjust the sensitivity - Current: > 15mA - Output type: Digital switch output (0, 1) - Suitable for watt-hour meter pulse data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
  16-Channel 12-bit PWM Servo Driver - I2C: You want to make a cool robot, maybe a hexapod walker, or maybe just a piece of art with a lot of moving parts. Or maybe you want to drive a lot of LEDs with precise PWM output. Using only two pins, control 16 free-running PWM outputs! You can even chain up 62 breakouts to control up to 992 PWM outputs.
