# Fritzing sketch OldSchematic (saved by Fritzing 0.8.7b)

parts:
  Mod1 = Raspberry Pi 4B
  Part1 = Arduino Uno (Rev3)
  BDLLC = Logic Level Converter [part_number="Logic Level Converter"]
  R1 = Basic Servo [part_number=Servo1]
  R2 = Basic Servo [part_number=Servo2]
  L1 = Basic Servo [part_number=Servo3]
  L2 = Basic Servo [part_number=Servo4]
  BATT1 = LiPoly Battery (1300mAh)
  7805 = Voltage Regulator - 5V [part_number="Voltage Regulator" package="TO220 [THT]"]
  Part5 = Arduino Uno (Rev3)
  DRV8833 = Adafruit DRV8833 DC/Stepper Motor Driver [part_number="Motor Driver"]
  DCL = Hobby Gearmotor with 48:1 gearbox [part_number=DC2]
  DCR = Hobby Gearmotor with 48:1 gearbox [part_number=DC1]
  hc-sr04 = HC-SR04 [part_number="Ultrasonic Sensors"]
  hc-sr2 = HC-SR04
  hc-sr3 = HC-SR04
  TCRT5000 = TCRT5000 digital module [part_number="Line Sensors"]
  TCRT3 = TCRT5000 digital module [part_number=151608]
  Part12 = Adafruit DRV8833 DC/Stepper Motor Driver [part_number="Adafruit #3297"]
  M1 = Stepper Motor - Bipolar

nets:
  N1: Mod1.3V3, BDLLC.LV
  N2: Mod1.GPIO14, BDLLC.TX_LV
  N3: Mod1.GPIO15, BDLLC.RX_LV
  GND: Mod1.GPIO23, Part1.GND, BDLLC.GND, hc-sr04.GND, TCRT3.GND
  N4: Part1.A4/SDA, Part5.A4/SDA
  N5: Part1.A5/SCL, Part5.A5/SCL
  N6: Part1.D8, hc-sr3.Trig
  N7: Part1.D9_PWM, hc-sr3.Echo
  N8: Part1.D10_PWM/SS, hc-sr2.Trig
  N9: Part1.D11_PWM/MOSI, hc-sr2.Echo
  N10: Part1.D12/MISO, hc-sr04.Trig
  N11: Part1.D13/SCK, hc-sr04.Echo
  N12: Part1.D0/RX, BDLLC.TX_HV
  N13: Part1.D1/TX, BDLLC.RX_HV
  N14: Part1.D2, DRV8833.AIN1
  N15: Part1.D3_PWM, DRV8833.AIN2
  N16: Part1.D4, DRV8833.BIN2
  N17: Part1.D5_PWM, DRV8833.BIN1
  N18: Part1.D6_PWM, TCRT5000.DO1
  N19: Part1.D7, TCRT3.DO1
  5V: Part1.5V, BDLLC.HV, TCRT3.VCC
  N20: R1.vcc, 7805.output_voltage, DRV8833.PWRIN
  N21: R1.pulse, Part5.D3_PWM
  N22: R2.pulse, Part5.D4
  N23: L1.pulse, Part5.D5_PWM
  N24: L2.pulse, Part5.D6_PWM
  N25: BATT1.positive, 7805.input_voltage
  GND_2: BATT1.negative, 7805.GND, DRV8833.GND
  N26: Part5.D8, Part12.AIN1
  N27: Part5.D9_PWM, Part12.AIN2
  N28: Part5.D10_PWM/SS, Part12.BIN2
  N29: Part5.D11_PWM/MOSI, Part12.BIN1
  N30: Part5.5V, Part12.!SLEEP
  N31: DRV8833.AOUT2, DCL.pin_1
  N32: DRV8833.AOUT1, DCL.pin_2
  N33: DRV8833.BOUT1, DCR.pin_2
  N34: DRV8833.BOUT2, DCR.pin_1
  VCC: hc-sr2.VCC, hc-sr3.VCC
  N35: Part12.AOUT2, M1.B
  N36: Part12.AOUT1, M1.D
  N37: Part12.BOUT1, M1.A
  N38: Part12.BOUT2, M1.C

custom parts:
  LiPoly Battery (1300mAh): Lithium Ion Polymer Battery (1300mAh)
  Adafruit DRV8833 DC/Stepper Motor Driver: Spin two DC motors or step one bi-polar or uni-polar stepper with up to 1.2A per channel using the DRV8833. This motor driver chip is a nice alternative to the TB6612 driver. Like that chip, you get 2 full H-bridges, but this chip is better for low voltage uses (can run from 2.7V up to 10.8V motor power) and has built in current limiting capability. We set it up for 1A current limiting so you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
  HC-SR04: This is a HC-SR04 Distance Sensor. This economical sensor provides 2cm to 400cm of non-contact measurement functionality with a ranging accuracy that can reach up to 3mm. Each HC-SR04 module includes an ultrasonic transmitter, a receiver and a control circuit. There are only four pins that you need to worry about on the HC-SR04: VCC (Power), Trig (Trigger), Echo (Receive), and GND (Ground).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
  TCRT5000 digital module: breakout board for TCRT5000 module, convert analog to digital - Uses TCRT5000 infrared reflectance sensor - Detection distance: 1mm~8mm - Focus distance: 2.5mm - Working voltage: 3.3V~12V - Uses wide voltage LM393 comparator - With multi-turn precision potentiometer to adjust the sensitivity - Current: > 15mA - Output type: Digital switch output (0, 1) - Suitable for watt-hour meter pulse data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
